# Fritzing sketch course 6 (1) (saved by Fritzing 1.0.5)
breadboards: 1

parts:
  LCD1 = LCD screen
  R1 = Rotary Potentiometer (Large) [maximum_resistance=10kΩ knob_status=50% power=0.5W package=THT]
  Part1 = Arduino Uno (Rev3)

nets:
  VSS: LCD1.VSS, LCD1.R/W, R1.leg2, Part1.GND
  VDD: LCD1.VDD, LCD1.LED+, R1.leg1, Part1.5V
  N1: LCD1.V0, R1.wiper
  N2: LCD1.RS, Part1.D12/MISO
  N3: LCD1.E, Part1.D11_PWM/MOSI
  N4: LCD1.DB4, Part1.D5_PWM
  N5: LCD1.DB5, Part1.D4
  N6: LCD1.DB6, Part1.D3_PWM
  N7: LCD1.DB7, Part1.D2
